// Logisim project SpencerJamesPrj1372.circ as structural Verilog: 8 circuits, main circuit main
module main (
);

  wire alu_1_zero, and_1_out, clock_1_out, instructionsplitter_1_p3, instructionsplitter_1_p4;
  wire [3:0] alucontrol_1_out_3;
  wire [4:0] instructionsplitter_1_p5, instructionsplitter_1_p6, instructionsplitter_1_p7, multiplexer_1_out;
  wire [5:0] register_1_q_2;
  wire [15:0] instructionsplitter_1_p2;
  wire [31:0] adder_1_out, adder_2_out, alu_1_out_5, bit_extender_1_out, datamemory_1_out_6,
       multiplexer_2_out, multiplexer_3_out, multiplexer_4_out, register_1_q, registers_1_out_7,
       registers_1_out_8, rom_1_data, shifter_1_out;

  Register #(.width(32)) register_1 (
    .D(multiplexer_3_out), .Q({register_1_q[31:8], register_1_q_2, register_1_q[1:0]}), .clk(clock_1_out));  // open: en, clr
  Clock clock_1 (.out(clock_1_out));
  Adder #(.width(32)) adder_1 (
    .a({register_1_q[31:8], register_1_q_2, register_1_q[1:0]}), .b(32'h4), .out(adder_1_out));  // open: cin, cout
  ROM #(.addrWidth(6), .dataWidth(32)) rom_1 (.addr(register_1_q_2), .data(rom_1_data));  // open: sel
  // InstructionSplitter instructionsplitter_1: pin names not known; wires that end beside it: rom_1_data, instructionsplitter_1_p2, instructionsplitter_1_p3, instructionsplitter_1_p4, instructionsplitter_1_p5, instructionsplitter_1_p6, instructionsplitter_1_p7
  Multiplexer #(.width(5)) multiplexer_1 (
    .in0(instructionsplitter_1_p6), .in1(instructionsplitter_1_p7), .out(multiplexer_1_out));  // open: sel, en
  Control control_1 ();  // open: RegWrite, ALUSrc, MemWrite, ALUOp, in_1, out_6, out_7, Branch, RegDst
  assign bit_extender_1_out = {{16{instructionsplitter_1_p2[15]}}, instructionsplitter_1_p2};  // Bit_Extender bit_extender_1
  Registers registers_1 (
    .Read_Reg1(instructionsplitter_1_p5), .Read_Reg2(instructionsplitter_1_p6), .in_5(multiplexer_4_out),
    .Write_Reg(multiplexer_1_out), .out_7(registers_1_out_7), .out_8(registers_1_out_8), .clock(clock_1_out));  // open: reg_write
  Multiplexer #(.width(32)) multiplexer_2 (
    .in0(registers_1_out_8), .in1(bit_extender_1_out), .out(multiplexer_2_out));  // open: sel, en
  Adder #(.width(32)) adder_2 (.a(adder_1_out), .b(shifter_1_out), .out(adder_2_out));  // open: cin, cout
  Shifter #(.width(32)) shifter_1 (.in(bit_extender_1_out), .\dist (5'b00010), .out(shifter_1_out));
  ALU alu_1 (
    .in_1(registers_1_out_7), .in_2(multiplexer_2_out), .out_5(alu_1_out_5), .Zero(alu_1_zero),
    .ALU_Operation(alucontrol_1_out_3));
  ALUControl alucontrol_1 (.out_3(alucontrol_1_out_3));  // open: ALUOp, Funct_Field
  Multiplexer #(.width(32)) multiplexer_3 (
    .in0(adder_1_out), .in1(adder_2_out), .out(multiplexer_3_out), .sel(and_1_out));  // open: en
  buf and_1 (and_1_out, alu_1_zero);  // AND_Gate
  DataMemory datamemory_1 (
    .clock(clock_1_out), .in_3(alu_1_out_5), .in_4(registers_1_out_8), .out_6(datamemory_1_out_6));  // open: MemWrite, in_5
  Multiplexer #(.width(32)) multiplexer_4 (
    .in0(alu_1_out_5), .in1(datamemory_1_out_6), .out(multiplexer_4_out));  // open: sel, en

  // Notes on the sheet:
  //   PC
  //   Program Memory
  //   Data
  //   Memory
endmodule

module ALU (
  input  [31:0] in_1,
  input  [31:0] in_2,
  input  [3:0] ALU_Operation,
  output Zero,
  output [31:0] out_5
);

  wire subtractor_1_bout;
  wire [31:0] adder_1_out, and_1_out, or_1_out, subtractor_1_out, xor_1_out;

  assign and_1_out = in_1 & in_1;  // AND_Gate and_1, 32 bits wide
  assign or_1_out = in_1 | in_1;  // OR_Gate or_1, 32 bits wide
  Adder #(.width(32)) adder_1 (.a(in_1), .b(in_1), .out(adder_1_out));  // open: cin, cout
  Multiplexer #(.select(4), .width(32), .enable("false")) multiplexer_1 (
    .in0(and_1_out), .in1(or_1_out), .in6(adder_1_out), .in7(subtractor_1_out), .in12(xor_1_out),
    .out(out_5), .sel(ALU_Operation));  // open: in2, in3, in4, in5, in8, in9, in10, in11, in13, in14, in15
  Subtractor #(.width(32)) subtractor_1 (
    .a(in_1), .b(in_1), .out(subtractor_1_out), .bout(subtractor_1_bout));  // open: bin
  Multiplexer #(.width(32), .enable("false")) multiplexer_2 (
    .in0({32{1'b0}}), .in1(32'h1), .sel(subtractor_1_bout));  // open: out
  Comparator #(.width(32)) comparator_1 (.a(in_1), .b(in_1));  // open: gt, eq, lt
  Comparator #(.width(32)) comparator_2 (.a({32{1'b0}}), .b(out_5), .eq(Zero));  // open: gt, lt
  assign xor_1_out = in_1 ^ in_1;  // XOR_Gate xor_1, 32 bits wide

  assign in_2 = in_1;

  // Notes on the sheet:
  //   ALU Result
endmodule

module Registers (
  input  clock,
  input  reg_write,
  input  [4:0] Read_Reg1,
  input  [4:0] Read_Reg2,
  input  [31:0] in_5,
  input  [4:0] Write_Reg,
  output [31:0] out_7,
  output [31:0] out_8
);


  // Notes on the sheet:
  //   Write Data
  //   Read Data 1
  //   Read Data 2
endmodule

module DataMemory (
  input  MemWrite,
  input  clock,
  input  [31:0] in_3,
  input  [31:0] in_4,
  input  in_5,
  output [31:0] out_6
);


  // Notes on the sheet:
  //   address
  //   in data
  //   MemRead
  //   out data
endmodule

module Control (
  input  [5:0] in_1,
  output RegWrite,
  output ALUSrc,
  output MemWrite,
  output [1:0] ALUOp,
  output out_6,
  output out_7,
  output Branch,
  output RegDst
);

  ROM #(.addrWidth(6), .dataWidth(9)) rom_1 (
    .addr(in_1), .data({RegDst, Branch, out_7, out_6, ALUOp, MemWrite, ALUSrc, RegWrite}));  // open: sel

  // Notes on the sheet:
  //   contents of rom_1 (hex, n*v repeats v):
  //   111 111 0 0 88 30*0 63 111 111 111 4*0 6
  //   MemToReg
  //   MemRead
endmodule

module ALUControl (
  input  [1:0] ALUOp,
  input  [5:0] Funct_Field,
  output [3:0] out_3
);

  wire and_1_out, and_2_out, and_3_out, and_4_out, and_5_out, and_6_out, and_7_out, not_1_out, not_2_out,
       not_3_out, not_4_out, not_5_out, not_6_out, not_7_out, not_8_out, not_9_out, not_10_out, not_11_out,
       not_12_out, not_13_out, not_14_out, not_15_out, not_16_out, not_17_out, not_18_out, not_19_out,
       not_20_out, not_21_out, not_22_out, not_23_out, not_24_out, not_25_out, not_26_out, not_27_out,
       or_1_out, or_2_out;
  wire [2:0] priority_encoder_1_out;

  or or_1 (or_1_out, and_1_out, and_2_out);
  and and_1 (and_1_out, not_2_out, not_1_out);
  not not_1 (not_1_out, ALUOp[0]);
  not not_2 (not_2_out, ALUOp[1]);
  and and_2 (and_2_out, ALUOp[1], not_3_out, Funct_Field[5], not_6_out, not_7_out, not_8_out, not_4_out, not_5_out);
  not not_3 (not_3_out, ALUOp[0]);
  not not_4 (not_4_out, Funct_Field[1]);
  not not_5 (not_5_out, Funct_Field[0]);
  not not_6 (not_6_out, Funct_Field[4]);
  not not_7 (not_7_out, Funct_Field[3]);
  not not_8 (not_8_out, Funct_Field[2]);
  and and_3 (and_3_out, not_9_out, ALUOp[0]);
  not not_9 (not_9_out, ALUOp[1]);
  or or_2 (or_2_out, and_3_out, and_4_out);
  and and_4 (and_4_out, ALUOp[1], not_10_out, Funct_Field[5], not_12_out, not_11_out, not_13_out, Funct_Field[1], not_14_out);
  not not_10 (not_10_out, ALUOp[0]);
  not not_11 (not_11_out, Funct_Field[3]);
  not not_12 (not_12_out, Funct_Field[4]);
  not not_13 (not_13_out, Funct_Field[2]);
  and and_5 (and_5_out, ALUOp[1], not_16_out, Funct_Field[5], not_15_out, not_18_out, Funct_Field[2], not_19_out, not_17_out);
  not not_14 (not_14_out, Funct_Field[0]);
  not not_15 (not_15_out, Funct_Field[4]);
  not not_16 (not_16_out, ALUOp[0]);
  not not_17 (not_17_out, Funct_Field[0]);
  not not_18 (not_18_out, Funct_Field[3]);
  not not_19 (not_19_out, Funct_Field[1]);
  not not_20 (not_20_out, ALUOp[0]);
  and and_6 (and_6_out, ALUOp[1], not_20_out, Funct_Field[5], not_21_out, not_23_out, Funct_Field[2], not_22_out, Funct_Field[0]);
  not not_21 (not_21_out, Funct_Field[4]);
  not not_22 (not_22_out, Funct_Field[1]);
  not not_23 (not_23_out, Funct_Field[3]);
  and and_7 (and_7_out, ALUOp[1], not_24_out, Funct_Field[5], not_25_out, Funct_Field[3], not_26_out, Funct_Field[1], not_27_out);
  not not_24 (not_24_out, ALUOp[0]);
  not not_25 (not_25_out, Funct_Field[4]);
  not not_26 (not_26_out, Funct_Field[2]);
  Priority_Encoder priority_encoder_1 (
    .in0(and_5_out), .in1(and_6_out), .in2(or_1_out), .in3(or_2_out), .in4(and_7_out),
    .out(priority_encoder_1_out));  // open: in5, in6, in7, en_in, gs, en_out
  not not_27 (not_27_out, Funct_Field[0]);
  Multiplexer #(.select(3), .width(4)) multiplexer_1 (
    .in0(4'b0000), .in1(4'b0001), .in2(4'b0010), .in3(4'b0110), .in4(4'b0111), .out(out_3),
    .sel(priority_encoder_1_out));  // open: in5, in6, in7, en
endmodule

module InstructionSplitter (
  input  [31:0] instr_in,
  output [5:0] out5_0,
  output [4:0] out15_11,
  output [4:0] out20_16,
  output [4:0] out25_21,
  output [5:0] out31_26,
  output [15:0] out15_0
);


  assign out5_0 = instr_in[5:0];
  assign out15_0 = instr_in[15:0];
  assign out15_11 = instr_in[15:11];
  assign out20_16 = instr_in[20:16];
  assign out25_21 = instr_in[25:21];
  assign out31_26 = instr_in[31:26];
endmodule

module Reg8 (
  input  in_1,
  input  in_2,
  input  [2:0] in_3,
  input  [2:0] in_4,
  input  [31:0] in_5,
  input  [2:0] in_6,
  output [31:0] out_7,
  output [31:0] out_8
);

  wire demultiplexer_1_out0, demultiplexer_1_out1, demultiplexer_1_out2, demultiplexer_1_out3,
       demultiplexer_1_out4, demultiplexer_1_out5, demultiplexer_1_out6, demultiplexer_1_out7;
  wire [31:0] register_1_q, register_2_q, register_3_q, register_4_q, register_5_q, register_6_q,
       register_7_q, register_8_q;

  Demultiplexer #(.select(3)) demultiplexer_1 (
    .out0(demultiplexer_1_out0), .out1(demultiplexer_1_out1), .out2(demultiplexer_1_out2),
    .out3(demultiplexer_1_out3), .out4(demultiplexer_1_out4), .out5(demultiplexer_1_out5),
    .out6(demultiplexer_1_out6), .out7(demultiplexer_1_out7), .in(in_2), .sel(in_6));  // open: en
  Register #(.width(32)) register_1 (.D(in_5), .en(demultiplexer_1_out0), .Q(register_1_q), .clk(in_1));  // open: clr
  Register #(.width(32)) register_2 (.D(in_5), .en(demultiplexer_1_out1), .Q(register_2_q), .clk(in_1));  // open: clr
  Register #(.width(32)) register_3 (.D(in_5), .en(demultiplexer_1_out2), .Q(register_3_q), .clk(in_1));  // open: clr
  Register #(.width(32)) register_4 (.D(in_5), .en(demultiplexer_1_out3), .Q(register_4_q), .clk(in_1));  // open: clr
  Register #(.width(32)) register_5 (.D(in_5), .en(demultiplexer_1_out4), .Q(register_5_q), .clk(in_1));  // open: clr
  Register #(.width(32)) register_6 (.D(in_5), .en(demultiplexer_1_out5), .Q(register_6_q), .clk(in_1));  // open: clr
  Register #(.width(32)) register_7 (.D(in_5), .en(demultiplexer_1_out6), .Q(register_7_q), .clk(in_1));  // open: clr
  Register #(.width(32)) register_8 (.D(in_5), .en(demultiplexer_1_out7), .Q(register_8_q), .clk(in_1));  // open: clr
  Multiplexer #(.select(3), .width(32)) multiplexer_1 (
    .in0(register_1_q), .in1(register_2_q), .in2(register_3_q), .in3(register_4_q), .in4(register_5_q),
    .in5(register_6_q), .in6(register_7_q), .in7(register_8_q), .out(out_7), .sel(in_3));  // open: en
  Multiplexer #(.select(3), .width(32)) multiplexer_2 (
    .in0(register_1_q), .in1(register_2_q), .in2(register_3_q), .in3(register_4_q), .in4(register_5_q),
    .in5(register_6_q), .in6(register_7_q), .in7(register_8_q), .out(out_8), .sel(in_4));  // open: en
endmodule
